// Logisim project VGA_driver.circ as structural Verilog: 8 circuits, main circuit main
module main (
);

  // clk_gen clk_gen_1: pin names not known
  // SRAM_controller sram_controller_1: pin names not known
endmodule

module h_clk_gen (
  output eo_bporch_264,
  output eo_vis_200,
  output eo_fporch_210,
  output eo_syncp_242,
  output wr_mode,
  output h_sync,
  output clk,
  output [7:0] j_addr
);

  wire j_k_ff_1_q, not_1_out, not_2_out, not_3_out, not_4_out, not_5_out, not_6_out, not_7_out, not_8_out,
       not_9_out, or_1_out;
  wire [7:1] line_counter_q_2;
  wire [8:8] line_counter_q;

  Clock xtal (.out(clk));
  Counter #(.max('h1ff), .width(9)) line_counter (
    .clr(eo_bporch_264), .load(1'b0), .up(1'b1), .count(1'b1), .clk(clk),
    .Q({line_counter_q[8], line_counter_q_2, wr_mode}));  // open: D, carry
  not not_1 (not_1_out, wr_mode);
  not not_2 (not_2_out, line_counter_q_2[1]);
  not not_3 (not_3_out, line_counter_q_2[2]);
  not not_4 (not_4_out, line_counter_q_2[3]);
  not not_5 (not_5_out, line_counter_q_2[4]);
  not not_6 (not_6_out, line_counter_q_2[5]);
  not not_7 (not_7_out, line_counter_q_2[6]);
  not not_8 (not_8_out, line_counter_q_2[7]);
  not not_9 (not_9_out, line_counter_q[8]);
  and and_1 (eo_vis_200, not_1_out, not_2_out, not_3_out, line_counter_q_2[3], not_5_out, not_6_out, line_counter_q_2[6], line_counter_q_2[7]);
  and and_2 (eo_fporch_210, not_1_out, line_counter_q_2[1], not_3_out, not_4_out, line_counter_q_2[4], not_6_out, line_counter_q_2[6], line_counter_q_2[7]);
  and and_3 (eo_syncp_242, not_1_out, line_counter_q_2[1], not_3_out, not_4_out, line_counter_q_2[4], line_counter_q_2[5], line_counter_q_2[6], line_counter_q_2[7]);
  and and_4 (eo_bporch_264, not_2_out, not_3_out, line_counter_q_2[3], not_5_out, not_6_out, not_7_out, not_8_out, line_counter_q[8]);
  J_K_Flip_Flop j_k_ff_1 (
    .J(eo_vis_200), .K(eo_vis_200), .clk(clk), .Q(j_k_ff_1_q), .preset(eo_bporch_264));  // open: Qn, reset
  Register register_1 (.D({line_counter_q_2, wr_mode}), .en(j_k_ff_1_q), .clk(clk), .Q(j_addr));  // open: clr
  or or_1 (or_1_out, eo_fporch_210, eo_syncp_242);
  J_K_Flip_Flop j_k_ff_2 (
    .J(or_1_out), .K(or_1_out), .clk(clk), .Q(h_sync), .preset(eo_bporch_264));  // open: Qn, reset
endmodule

module v_clk_gen (
  input  line_done,
  output eo_vis_600,
  output eo_fporch_601,
  output eo_syncp_605,
  output eo_bporch_628,
  output [7:0] i_addr,
  output v_sync
);

  wire is_600_or_601_out, j_k_ff_1_q, not_1_out, not_2_out, not_3_out, not_4_out, not_5_out, not_6_out,
       not_7_out, not_8_out, not_9_out, not_10_out, or_1_out;
  wire [9:0] counter_1_q;

  Counter #(.max('h3ff), .width(10)) counter_1 (
    .clr(eo_bporch_628), .load(1'b0), .up(1'b1), .count(1'b1), .clk(line_done), .Q(counter_1_q));  // open: D, carry
  not not_1 (not_1_out, counter_1_q[0]);
  not not_2 (not_2_out, counter_1_q[1]);
  not not_3 (not_3_out, counter_1_q[2]);
  not not_4 (not_4_out, counter_1_q[3]);
  not not_5 (not_5_out, counter_1_q[4]);
  not not_6 (not_6_out, counter_1_q[5]);
  not not_7 (not_7_out, counter_1_q[6]);
  not not_8 (not_8_out, counter_1_q[7]);
  not not_9 (not_9_out, counter_1_q[8]);
  not not_10 (not_10_out, counter_1_q[9]);
  and and_1 (eo_vis_600, is_600_or_601_out, not_1_out);
  and is_600_or_601 (is_600_or_601_out, not_2_out, not_3_out, counter_1_q[3], counter_1_q[4], not_6_out, counter_1_q[6], not_8_out, not_9_out, counter_1_q[9]);
  and and_2 (eo_fporch_601, is_600_or_601_out, counter_1_q[0]);
  and and_3 (eo_syncp_605, counter_1_q[0], not_2_out, counter_1_q[2], counter_1_q[3], counter_1_q[4], not_6_out, counter_1_q[6], not_8_out, not_9_out, counter_1_q[9]);
  and and_4 (eo_bporch_628, counter_1_q[2], not_4_out, counter_1_q[4], counter_1_q[5], counter_1_q[6], not_8_out, not_9_out, counter_1_q[9]);
  J_K_Flip_Flop j_k_ff_1 (
    .J(eo_vis_600), .K(eo_vis_600), .clk(line_done), .Q(j_k_ff_1_q), .preset(eo_bporch_628));  // open: Qn, reset
  Register register_1 (.D(counter_1_q[9:2]), .en(j_k_ff_1_q), .clk(line_done), .Q(i_addr));  // open: clr
  or or_1 (or_1_out, eo_fporch_601, eo_syncp_605);
  J_K_Flip_Flop j_k_ff_2 (
    .J(or_1_out), .K(or_1_out), .clk(line_done), .Q(v_sync), .preset(eo_bporch_628));  // open: Qn, reset
endmodule

module clk_gen (
  output clk,
  output wr_mode,
  output [7:0] i_addr,
  output [7:0] j_addr,
  output h_sync,
  output v_sync
);

  wire h_clk_gen_1_eo_bporch_264;

  h_clk_gen h_clk_gen_1 (
    .eo_bporch_264(h_clk_gen_1_eo_bporch_264), .wr_mode(wr_mode), .h_sync(h_sync), .clk(clk), .j_addr(j_addr));  // open: eo_vis_200, eo_fporch_210, eo_syncp_242
  v_clk_gen v_clk_gen_1 (
    .line_done(h_clk_gen_1_eo_bporch_264), .i_addr(i_addr), .v_sync(v_sync));  // open: eo_vis_600, eo_fporch_601, eo_syncp_605, eo_bporch_628
endmodule

module SRAM_controller (
  input  wbit_0,
  input  r_bank,
  output RAM0_CE,
  output RAM0_WE,
  output RAM1_CE,
  output RAM1_WE
);

  wire not_1_out, not_2_out;

  not not_1 (not_1_out, wbit_0);
  not not_2 (not_2_out, r_bank);
  nand nand_1 (RAM0_CE, wbit_0, r_bank);
  and and_1 (RAM0_WE, r_bank, not_1_out);
  or or_1 (RAM1_CE, wbit_0, r_bank);
  and and_2 (RAM1_WE, not_2_out, wbit_0);
endmodule

module bus_mux (
  input  [7:0] r_h_addr,
  input  [7:0] r_v_addr,
  input  [7:0] w_h_addr,
  input  [7:0] w_v_addr,
  input  [7:0] w_data,
  output RAM0_CE,
  output RAM0_WE,
  output RAM1_CE,
  output RAM1_WE,
  output [14:0] RAM_a_addr,
  output [14:0] RAM_b_addr,
  output r_bank,
  output [7:0] RAM0_data_w,
  output [7:0] RAM1_data_w
);

  wire not_1_out, wbit_0;
  wire [14:0] addr_combiner_1_addr, addr_combiner_2_addr;

  addr_combiner addr_combiner_1 (.v_addr(w_h_addr), .h_addr(w_v_addr), .bank_sel(wbit_0), .addr(addr_combiner_1_addr));
  addr_combiner addr_combiner_2 (.v_addr(r_h_addr), .h_addr(r_v_addr), .bank_sel(r_bank), .addr(addr_combiner_2_addr));
  not not_1 (not_1_out, r_bank);
  assign RAM1_data_w = not_1_out ? w_data : 8'bz;  // Controlled_Buffer controlled_buffer_1
  assign RAM0_data_w = r_bank ? w_data : 8'bz;  // Controlled_Buffer controlled_buffer_2
  Multiplexer #(.width(15)) multiplexer_1 (
    .in0(addr_combiner_2_addr), .in1(addr_combiner_1_addr), .out(RAM_a_addr), .sel(r_bank));
  Multiplexer #(.width(15)) multiplexer_2 (
    .in0(addr_combiner_1_addr), .in1(addr_combiner_2_addr), .out(RAM_b_addr), .sel(r_bank));
  SRAM_controller sram_controller_1 (
    .wbit_0(wbit_0), .r_bank(r_bank), .RAM0_CE(RAM0_CE), .RAM0_WE(RAM0_WE), .RAM1_CE(RAM1_CE),
    .RAM1_WE(RAM1_WE));
endmodule

module SRAM_module (
  output [7:0] RAM_data_r
);

  wire bus_mux_1_r_bank, bus_mux_1_ram0_ce, bus_mux_1_ram0_we, bus_mux_1_ram1_ce, bus_mux_1_ram1_we,
       not_1_out, not_2_out;
  wire [7:0] bus_mux_1_ram0_data_w, bus_mux_1_ram1_data_w, controlled_buffer_3_out, controlled_buffer_4_out,
       ram_1_data, ram_2_data;
  wire [14:0] bus_mux_1_ram_a_addr, bus_mux_1_ram_b_addr;

  bus_mux bus_mux_1 (
    .RAM0_CE(bus_mux_1_ram0_ce), .RAM0_WE(bus_mux_1_ram0_we), .RAM1_CE(bus_mux_1_ram1_ce),
    .RAM1_WE(bus_mux_1_ram1_we), .RAM_a_addr(bus_mux_1_ram_a_addr), .RAM_b_addr(bus_mux_1_ram_b_addr),
    .r_bank(bus_mux_1_r_bank), .RAM0_data_w(bus_mux_1_ram0_data_w), .RAM1_data_w(bus_mux_1_ram1_data_w));  // open: r_h_addr, r_v_addr, w_h_addr, w_v_addr, w_data
  RAM #(.addrWidth(15), .databus("bidir"), .enables("line"), .\type ("nonvolatile")) ram_1 (
    .addr(bus_mux_1_ram_a_addr), .we(bus_mux_1_ram1_we), .oe(bus_mux_1_ram1_ce), .data(ram_1_data));  // open: clk
  RAM #(.addrWidth(15), .databus("bidir"), .enables("line")) ram_2 (
    .addr(bus_mux_1_ram_b_addr), .we(bus_mux_1_ram0_we), .oe(bus_mux_1_ram0_ce), .data(ram_2_data));  // open: clk
  assign ram_1_data = not_1_out ? bus_mux_1_ram0_data_w : 8'bz;  // Controlled_Buffer controlled_buffer_1
  assign ram_2_data = not_2_out ? bus_mux_1_ram1_data_w : 8'bz;  // Controlled_Buffer controlled_buffer_2
  not not_1 (not_1_out, bus_mux_1_ram1_we);
  assign controlled_buffer_3_out = bus_mux_1_ram1_we ? ram_1_data : 8'bz;  // Controlled_Buffer controlled_buffer_3
  not not_2 (not_2_out, bus_mux_1_ram0_we);
  assign controlled_buffer_4_out = bus_mux_1_ram0_we ? ram_2_data : 8'bz;  // Controlled_Buffer controlled_buffer_4
  Multiplexer #(.width(8)) multiplexer_1 (
    .in0(controlled_buffer_3_out), .in1(controlled_buffer_4_out), .out(RAM_data_r), .sel(bus_mux_1_r_bank));
endmodule

module addr_combiner (
  input  [7:0] v_addr,
  input  [7:0] h_addr,
  output bank_sel,
  output [14:0] addr
);


  assign addr = {h_addr, v_addr[7:1]};
  assign bank_sel = v_addr[0];
endmodule
